# Fritzing sketch diagram (saved by Fritzing 0.9.9b)

parts:
  Mod1 = Raspberry Pi Pico
  S1 = Pushbutton [package="[THT]"]
  Part1 = ws2812b [package="smd 2812b"]

nets:
  N1: Mod1.pin_13, Mod1.pin_32, Mod1.pin_33, Mod1.pin_38, S1.Pin_3, S1.Pin_4, Part1.VSS
  N2: Mod1.pin_34, Part1.DIN
  N3: Mod1.pin_40, Part1.VDD

custom parts:
  Raspberry Pi Pico: Raspberry Pi Pico. Based around the RP2040 microcontroller the Pico is a low cost microcontroller device bringing Raspberry Pi quality, cost, and easy of use to the microcontroller space. Jan 2021, Split part in to two versions: tht (this one) and SMD. This one will drill holes for a .1 in header in pcb to allow plugging in the module as well as providing pads to solder the module to the top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
